# Fritzing sketch RC car project (saved by Fritzing 0.9.3b)
breadboards: 1

parts:
  Part1 = Arduino Uno (Rev3)
  IC1 = H-Bridge [package=THT]
  M2 = DC Motor
  M1 = DC Motor
  VCC1 = Battery

nets:
  N1: Part1.D9_PWM, IC1.4A
  N2: Part1.D3_PWM, IC1.1A
  N3: Part1.D5_PWM, IC1.2A
  N4: Part1.D6_PWM, IC1.3A
  N5: Part1.5V, IC1.1_2EN, IC1.3_4EN, IC1.VCC1
  GND: Part1.GND, IC1.GND1, IC1.GND2, IC1.GND3, IC1.GND4, VCC1.-
  N6: IC1.1Y, M1.pin_2
  N7: IC1.2Y, M1.pin_1
  N8: IC1.VCC2, VCC1.+
  N9: IC1.3Y, M2.pin_2
  N10: IC1.4Y, M2.pin_1
